// Logisim project Circuitos do Experimento 2 - Atualizado.circ as structural Verilog: 1 circuit, main circuit main
module main (
  input  A,
  input  B,
  input  V
);

  wire and_1_out, and_2_out, and_3_out, and_4_out, and_5_out, and_6_out, and_7_out, and_8_out, nor_1_out,
       nor_2_out, not_1_out, not_2_out, not_3_out, not_4_out, not_5_out, not_6_out, not_7_out, or_1_out,
       or_2_out, or_3_out;

  not not_1 (not_1_out, V);
  not not_2 (not_2_out, A);
  and and_1 (and_1_out, B, not_1_out);
  not not_3 (not_3_out, A);
  and and_2 (and_2_out, B, V);
  not not_4 (not_4_out, B);
  and and_3 (and_3_out, not_2_out, and_1_out);
  and and_4 (and_4_out, not_3_out, and_2_out);
  not not_5 (not_5_out, A);
  not not_6 (not_6_out, A);
  nor nor_1 (nor_1_out, B, V);
  not not_7 (not_7_out, A);
  and and_5 (and_5_out, not_4_out, V);
  and and_6 (and_6_out, not_5_out, B);
  and and_7 (and_7_out, not_6_out, V);
  nor nor_2 (nor_2_out, nor_1_out, A);
  and and_8 (and_8_out, not_7_out, and_5_out);
  or or_1 (or_1_out, and_3_out, and_4_out);
  or or_2 (or_2_out, and_6_out, and_7_out);
  LED R (.in(nor_2_out));
  LED R_2 (.in(or_3_out));
  or or_3 (or_3_out, and_8_out, or_1_out);
  LED R_3 (.in(or_2_out));

  // Notes on the sheet:
  //   Circuito da saida R simplificado: A̅B + A̅V
  //   Circuito da saida R com apenas um CI: ( A+ (B+V)' )'
  //   Circuito da saida R sem simplificação:   A̅B̅V + A̅BV̅+ A̅BV
endmodule
