// Logisim project Circuito do Experimento 3 - Atualizado.circ as structural Verilog: 1 circuit, main circuit main
// b2
module main (
  input  A,
  input  B,
  input  C
);

  wire and_1_out, and_2_out, and_3_out, and_4_out, not_1_out, not_2_out, not_3_out, not_4_out, or_1_out,
       or_2_out, or_3_out, or_4_out, or_5_out, xor_1_out;

  or or_1 (or_1_out, A, B);
  not not_1 (not_1_out, B);
  not not_2 (not_2_out, A);
  not not_3 (not_3_out, B);
  not not_4 (not_4_out, C);
  xor xor_1 (xor_1_out, A, C);
  and and_1 (and_1_out, not_1_out, C);
  and and_2 (and_2_out, not_2_out, not_3_out);
  and and_3 (and_3_out, and_2_out, C);
  and and_4 (and_4_out, B, not_4_out);
  or or_2 (or_2_out, xor_1_out, B);
  or or_3 (or_3_out, or_1_out, C);
  or or_4 (or_4_out, A, and_1_out);
  or or_5 (or_5_out, and_3_out, and_4_out);
  _7_Segment_Display u_7_segment_display_1 (
    .g(or_5_out), .e(or_2_out), .d(or_3_out), .c(or_4_out));  // open: f, a, b, dp

  // Notes on the sheet:
  //   Circuito A
  //   Circuito B
  //   Circuto C
  //   Circuito D
endmodule
