// Logisim project Circuito do Experimento 4 - Atualizado.circ as structural Verilog
module Experimento_04_7fb12fed (
  input  a1,
  input  a0,
  input  b1,
  input  b0,
  output NOT_BL
);

  wire and_1_out, bcd_1_centro, bcd_1_infdire, bcd_1_infesq, bcd_1_norte, bcd_1_sul, bcd_1_supdire,
       bcd_1_supesq, not_1_out, not_2_out, not_3_out, or_1_out, or_2_out, or_3_out, y0, y1, y2, y3;

  and and_1 (and_1_out, b1, a1);
  and and_2 (y0, b0, a0);
  not not_1 (not_1_out, b0);
  not not_2 (not_2_out, a0);
  or or_1 (or_1_out, not_1_out, not_2_out);
  and and_3 (y3, and_1_out, y0);
  and and_4 (y2, and_1_out, or_1_out);
  or or_2 (or_2_out, a1, a0);
  or or_3 (or_3_out, b1, b0);
  not not_3 (not_3_out, b0);
  or or_4 (NOT_BL, or_2_out, or_3_out);
  Multiplexer #(.enable("true"), .select(3)) multiplexer_1 (
    .in0(1'b0), .in1(1'b0), .in2(1'b0), .in3(1'b1), .in4(b0), .in5(b0), .in6(b0), .in7(not_3_out), .out(y1),
    .sel({a1, a0, b1}), .en(1'b1));
  BCD bcd_1 (
    .D(y3), .C(y2), .B(y1), .A(y0), .SupEsq(bcd_1_supesq), .Norte(bcd_1_norte), .SupDire(bcd_1_supdire),
    .InfDire(bcd_1_infdire), .Sul(bcd_1_sul), .InfEsq(bcd_1_infesq), .Centro(bcd_1_centro));
  _7_Segment_Display u_7_segment_display_1 (
    .g(bcd_1_centro), .f(bcd_1_supesq), .a(bcd_1_norte), .b(bcd_1_supdire), .e(bcd_1_infesq), .d(bcd_1_sul),
    .c(bcd_1_infdire));  // open: dp
endmodule

module BCD (
  input  D,
  input  C,
  input  B,
  input  A,
  output SupEsq,
  output Norte,
  output SupDire,
  output InfDire,
  output Sul,
  output InfEsq,
  output Centro
);

  wire and_1_out, and_2_out, and_3_out, and_4_out, and_5_out, and_6_out, and_7_out, and_8_out, and_9_out,
       and_10_out, and_11_out, and_12_out, and_13_out, and_14_out, and_15_out, and_16_out, and_17_out,
       not_1_out, not_2_out, not_3_out, not_4_out, not_5_out, not_6_out, not_7_out, not_8_out, not_9_out,
       not_10_out, not_11_out, not_12_out, not_13_out, not_14_out, not_15_out, not_16_out, not_17_out,
       not_18_out, not_19_out, not_20_out, not_21_out, not_22_out;

  not not_1 (not_1_out, B);
  not not_2 (not_2_out, A);
  not not_3 (not_3_out, B);
  not not_4 (not_4_out, A);
  not not_5 (not_5_out, C);
  not not_6 (not_6_out, A);
  not not_7 (not_7_out, C);
  not not_8 (not_8_out, B);
  not not_9 (not_9_out, A);
  not not_10 (not_10_out, B);
  not not_11 (not_11_out, C);
  not not_12 (not_12_out, A);
  not not_13 (not_13_out, C);
  not not_14 (not_14_out, A);
  not not_15 (not_15_out, B);
  not not_16 (not_16_out, C);
  not not_17 (not_17_out, A);
  not not_18 (not_18_out, A);
  not not_19 (not_19_out, C);
  not not_20 (not_20_out, B);
  not not_21 (not_21_out, A);
  and and_1 (and_1_out, not_1_out, not_2_out);
  and and_2 (and_2_out, C, not_3_out);
  and and_3 (and_3_out, C, not_4_out);
  and and_4 (and_4_out, not_5_out, not_6_out);
  and and_5 (and_5_out, not_7_out, B);
  and and_6 (and_6_out, C, A);
  not not_22 (not_22_out, C);
  and and_7 (and_7_out, not_8_out, not_9_out);
  and and_8 (and_8_out, B, A);
  or or_1 (InfDire, not_10_out, A, C);
  and and_9 (and_9_out, not_11_out, not_12_out);
  and and_10 (and_10_out, not_13_out, B);
  and and_11 (and_11_out, B, not_14_out);
  and and_12 (and_12_out, C, not_15_out, A);
  and and_13 (and_13_out, not_16_out, not_17_out);
  and and_14 (and_14_out, B, not_18_out);
  and and_15 (and_15_out, not_19_out, B);
  and and_16 (and_16_out, C, not_20_out);
  and and_17 (and_17_out, C, not_21_out);
  or or_2 (SupEsq, and_1_out, and_2_out, and_3_out, D);
  or or_3 (Norte, and_4_out, and_5_out, and_6_out, D);
  or or_4 (SupDire, not_22_out, and_7_out, and_8_out);
  or or_5 (Sul, and_9_out, and_10_out, and_11_out, and_12_out);
  or or_6 (InfEsq, and_13_out, and_14_out);
  or or_7 (Centro, and_15_out, and_16_out, and_17_out, D);
endmodule
