// Logisim project Circuito Experimento 5.circ as structural Verilog: 1 circuit, main circuit main
module main (
  input  op,
  input  A2,
  input  A1,
  input  A0,
  input  B2,
  input  B1,
  input  B0,
  output O
);

  wire adder_1_cout, adder_1_out, adder_3_cout, adder_3_out, adder_4_cout, adder_4_out, multiplexer_1_out,
       xor_1_out, xor_2_out, xor_3_out, xor_4_out;
  wire [2:2] adder_2_out;

  xor xor_1 (xor_1_out, op, B2);
  LED led_1 (.in(adder_1_out));
  Adder #(.width(1)) adder_1 (.a(A2), .b(xor_1_out), .out(adder_1_out), .cin(adder_3_cout), .cout(adder_1_cout));
  Adder #(.width(1)) adder_2 (.a(1'b0), .b(1'b0), .out(adder_2_out[2]), .cin(adder_1_cout), .cout(O));
  xor xor_2 (xor_2_out, op, B1);
  LED led_2 (.in(adder_3_out));
  Adder #(.width(1)) adder_3 (.a(A1), .b(xor_2_out), .out(adder_3_out), .cin(adder_4_cout), .cout(adder_3_cout));
  xor xor_3 (xor_3_out, op, B0);
  Adder #(.width(1)) adder_4 (.a(A0), .b(xor_3_out), .out(adder_4_out), .cin(op), .cout(adder_4_cout));
  Multiplexer #(.select(3)) multiplexer_1 (
    .in0(adder_1_out), .in2(1'b0), .in3(1'b1), .in4(1'b0), .in5(1'b1), .in7(adder_1_out),
    .out(multiplexer_1_out), .sel({adder_2_out[2], B2, A2}), .en(1'b1));  // open: in1, in6
  LED led_3 (.in(adder_4_out));
  LED led_4 (.in(xor_4_out));
  xor xor_4 (xor_4_out, adder_2_out[2], multiplexer_1_out);

  // Notes on the sheet:
  //   C_out 2
  //   S2 
  //   S3=Cout 
  //   C_out 1
  //   S2 
  //   A2
  //   S1 
  //   C_out 0
  //   Overflow
  //   S0 
endmodule
