// Logisim project Circuito Experimento 08.circ as structural Verilog: 4 circuits, main circuit Mux 4
module Mux_4 (
  input  I0,
  input  I1,
  input  I2,
  input  I3,
  input  S1,
  input  S0,
  output F
);

  wire and_1_out, and_2_out, and_3_out, and_4_out, not_1_out, not_2_out, not_3_out, not_4_out;

  and and_1 (and_1_out, I0, not_1_out, not_2_out);
  not not_1 (not_1_out, S1);
  not not_2 (not_2_out, S0);
  and and_2 (and_2_out, I1, not_3_out, S0);
  not not_3 (not_3_out, S1);
  and and_3 (and_3_out, I2, S1, not_4_out);
  not not_4 (not_4_out, S0);
  and and_4 (and_4_out, I3, S1, S0);
  or or_1 (F, and_1_out, and_2_out, and_3_out, and_4_out);
endmodule

module Mux8 (
  input  I0,
  input  I1,
  input  I2,
  input  I3,
  input  I4,
  input  I5,
  input  I6,
  input  I7,
  input  S2,
  input  S1,
  input  S0,
  output Z
);

  wire mux_4_1_f, mux_4_2_f;

  Mux_4 mux_4_1 (.I0(I0), .I1(I1), .I2(I2), .I3(I3), .S1(S1), .S0(S0), .F(mux_4_1_f));
  Mux_4 mux_4_2 (.I0(I4), .I1(I5), .I2(I6), .I3(I7), .S1(S1), .S0(S0), .F(mux_4_2_f));
  Mux_4 mux_4_3 (.I0(mux_4_1_f), .I3(mux_4_2_f), .S1(S2), .S0(S2), .F(Z));  // open: I1, I2
endmodule

module experimento_8 (
  input  P1,
  input  P2,
  input  P3
);

  wire button_1_out, CLK, Cout, Cout_t, J0, J1, K0, K1, not_1_out, not_2_out, P12, Q0, Q0_t, Q1, Q1_t;

  Button button_1 (.out(button_1_out));
  or or_1 (P12, P1, P2);
  Clock clock_1 (.out(CLK));
  J_K_Flip_Flop j_k_ff_1 (
    .J(J1), .clk(CLK), .K(K1), .Q(Q1), .Qn(Q1_t), .preset(1'b0), .reset(button_1_out));  // open: en
  Mux8 mux8_1 (
    .I0(1'b0), .I1(1'b1), .I2(1'b0), .I3(1'b0), .I4(1'b0), .I5(1'b1), .I6(1'b0), .I7(Cout_t), .S2(Q0),
    .S1(P12), .S0(P3), .Z(J1));
  Mux8 mux8_2 (
    .I0(1'b1), .I1(1'b0), .I2(1'b1), .I3(1'b0), .I4(1'b1), .I5(1'b0), .I6(1'b1), .I7(Cout_t), .S2(Q0),
    .S1(P12), .S0(P3), .Z(K1));
  LED S1 (.in(Q1_t));
  LED S3 (.in(Q1));
  J_K_Flip_Flop j_k_ff_2 (
    .J(J0), .clk(CLK), .K(K0), .Q(Q0), .Qn(Q0_t), .preset(1'b0), .reset(button_1_out));  // open: en
  and and_1 (J0, P12, P3);
  LED S2 (.in(Q1_t));
  or or_2 (K0, not_2_out, not_1_out);
  not not_1 (not_1_out, P3);
  not not_2 (not_2_out, P12);
  LED S1_2 (.in(Q1_t));
  LED S2_2 (.in(Q1_t));
  LED S3_2 (.in(Q1));
  Contador contador_1 (.B_D(Q1_t), .Preset(Q0_t), .Clock(CLK), .Cout(Cout));
  Contador contador_2 ();  // open: B_D, Preset, Clock, Cout
  not not_3 (Cout_t, Cout);
  Multiplexer #(.select(3)) multiplexer_1 (
    .in0(1'b0), .in1(1'b1), .in2(1'b0), .in3(1'b0), .in4(1'b0), .in5(1'b1), .in6(1'b0), .in7(Cout_t),
    .out(J1), .sel({Q0, P12, P3}));  // open: en
  Multiplexer #(.select(3)) multiplexer_2 (
    .in0(1'b1), .in1(1'b0), .in2(1'b1), .in3(1'b0), .in4(1'b1), .in5(1'b0), .in6(1'b1), .in7(Cout_t),
    .out(K1), .sel({Q0, P12, P3}));  // open: en

  // Notes on the sheet:
  //   Mux8
  //   Q1
  //   Mux 8
  //   Q0
  //   Semaforos:
  //   Semaforos:
  //   cd4029 contador
  //   Q1/ é o Binary/Decade
  //   Q0/ é o preset, ativa a contagem
endmodule

module Contador (
  input  B_D,
  input  Preset,
  input  Clock,
  output Cout
);

  wire counter_1_carry, counter_2_carry, not_1_out, or_1_out, or_2_out, or_3_out;

  not not_1 (not_1_out, B_D);
  Counter #(.width(4), .max('h9)) counter_1 (
    .load(1'b0), .D(4'b0000), .count(not_1_out), .carry(counter_1_carry), .clk(Clock), .clr(or_1_out));  // open: Q
  or or_1 (or_1_out, B_D, Preset);
  Counter #(.width(6), .max('hf)) counter_2 (
    .load(1'b0), .D({6{1'b0}}), .count(B_D), .carry(counter_2_carry), .clk(Clock), .clr(or_2_out));  // open: Q
  or or_2 (or_2_out, not_1_out, Preset);
  or or_3 (or_3_out, counter_1_carry, counter_2_carry);
  not not_2 (Cout, or_3_out);
endmodule
